// Logisim project puste brameczki.circ as structural Verilog
module AND (
  input  in_1,
  input  in_2,
  output out_3
);

  wire nand_1_out;

  nand nand_1 (nand_1_out, in_1, in_2);
  NOT not_1 (.in_1(nand_1_out), .out_2(out_3));
endmodule

module NOT (
  input  in_1,
  output out_2
);

  nand nand_1 (out_2, in_1, in_1);
endmodule

module OR (
  input  in_1,
  input  in_2,
  output out_3
);

  wire not_1_out_2, not_2_out_2;

  NOT not_1 (.in_1(in_1), .out_2(not_1_out_2));
  NOT not_2 (.in_1(in_2), .out_2(not_2_out_2));
  nand nand_1 (out_3, not_1_out_2, not_2_out_2);
endmodule

module NOR (
  input  in_1,
  input  in_2,
  output out_3
);

  wire or_1_out_3;

  NOT not_1 (.in_1(or_1_out_3), .out_2(out_3));
  OR or_1 (.in_1(in_1), .in_2(in_2), .out_3(or_1_out_3));
endmodule

module XOR (
  input  in_1,
  input  in_2,
  output out_3
);

  wire nand_1_out, nand_2_out, nand_3_out;

  nand nand_1 (nand_1_out, in_1, in_2);
  nand nand_2 (nand_2_out, in_1, nand_1_out);
  nand nand_3 (nand_3_out, nand_1_out, in_2);
  nand nand_4 (out_3, nand_2_out, nand_3_out);
endmodule
