// Logisim project syc7 zad1 nie dziala.circ as structural Verilog: 15 circuits, main circuit main
module main (
  input  A,
  input  B,
  input  C,
  input  A_2,
  input  B_2,
  input  C_2,
  output out_7,
  output out_8
);

  wire and_nand_1_out_3, and_nand_2_out_3, and_nand_3_out_3, and_nand_4_out_3, and_nand_5_out_3,
       and_nand_6_out_3, not_nand_1_out_2, xor_nand_1_out_3, xor_nand_2_out_3, xor_nand_3_out_3;

  AND_NAND and_nand_1 (.in_1(A), .in_2(and_nand_2_out_3), .out_3(and_nand_1_out_3));
  AND_NAND and_nand_2 (.in_1(B), .in_2(C), .out_3(and_nand_2_out_3));
  NOT_NAND not_nand_1 (.in_1(C_2), .out_2(not_nand_1_out_2));
  AND_NAND and_nand_3 (.in_1(A), .in_2(B), .out_3(and_nand_3_out_3));
  AND_NAND and_nand_4 (.in_1(B), .in_2(C), .out_3(and_nand_4_out_3));
  AND_NAND and_nand_5 (.in_1(A_2), .in_2(not_nand_1_out_2), .out_3(and_nand_5_out_3));
  AND_NAND and_nand_6 (.in_1(B_2), .in_2(C_2), .out_3(and_nand_6_out_3));
  XOR_NAND xor_nand_1 (.in_1(A), .in_2(and_nand_3_out_3), .out_3(xor_nand_1_out_3));
  XOR_NAND xor_nand_2 (.in_1(xor_nand_1_out_3), .in_2(and_nand_3_out_3), .out_3(xor_nand_2_out_3));
  OR_NAND or_nand_1 (.in_1(and_nand_5_out_3), .in_2(and_nand_6_out_3), .out_3(out_8));
  XOR_NAND xor_nand_3 (.in_1(xor_nand_2_out_3), .in_2(and_nand_4_out_3), .out_3(xor_nand_3_out_3));
  XOR_NAND xor_nand_4 (.in_1(xor_nand_3_out_3), .in_2(and_nand_1_out_3), .out_3(out_7));
endmodule

module AND_NAND (
  input  in_1,
  input  in_2,
  output out_3
);

  wire nand_1_out;

  nand nand_1 (nand_1_out, in_1, in_2);
  NOT_NAND not_nand_1 (.in_1(nand_1_out), .out_2(out_3));
endmodule

module NOT_NAND (
  input  in_1,
  output out_2
);

  nand nand_1 (out_2, in_1, in_1);
endmodule

module OR_NAND (
  input  in_1,
  input  in_2,
  output out_3
);

  wire not_nand_1_out_2, not_nand_2_out_2;

  NOT_NAND not_nand_1 (.in_1(in_1), .out_2(not_nand_1_out_2));
  NOT_NAND not_nand_2 (.in_1(in_2), .out_2(not_nand_2_out_2));
  nand nand_1 (out_3, not_nand_1_out_2, not_nand_2_out_2);
endmodule

module NOR_NAND (
  input  in_1,
  input  in_2,
  output out_3
);

  wire or_nand_1_out_3;

  NOT_NAND not_nand_1 (.in_1(or_nand_1_out_3), .out_2(out_3));
  OR_NAND or_nand_1 (.in_1(in_1), .in_2(in_2), .out_3(or_nand_1_out_3));
endmodule

module XOR_NAND (
  input  in_1,
  input  in_2,
  output out_3
);

  wire nand_1_out, nand_2_out, nand_3_out;

  nand nand_1 (nand_1_out, in_1, in_2);
  nand nand_2 (nand_2_out, in_1, nand_1_out);
  nand nand_3 (nand_3_out, nand_1_out, in_2);
  nand nand_4 (out_3, nand_2_out, nand_3_out);
endmodule

module NAND_NAND (
  input  in_1,
  input  in_2,
  output out_3
);

  nand nand_1 (out_3, in_1, in_2);
endmodule

module zad1 (
  input  A,
  input  B,
  input  C,
  output out_4,
  output out_5
);

  wire and_nand_1_out_3, not_nand_1_out_2;

  NOT_NAND not_nand_1 (.in_1(C), .out_2(not_nand_1_out_2));
  AND_NAND and_nand_1 (.in_1(A), .in_2(not_nand_1_out_2), .out_3(and_nand_1_out_3));
  AND_NAND and_nand_2 (.in_1(B), .in_2(C), .out_3(out_5));
  OR_NAND or_nand_1 (.in_1(and_nand_1_out_3), .in_2(out_5), .out_3(out_4));
endmodule

module zad2 (
  input  Lewy_czujnik,
  input  Srodkowy_czujnik,
  input  Prawy_czujnik,
  output lewy_silnik,
  output prawy_silnik
);

  wire and_nor_1_out_3, and_nor_2_out_3, and_nor_3_out_3, and_nor_4_out_3, not_nor_1_out_2, not_nor_2_out_2,
       not_nor_3_out_2, not_nor_4_out_2, not_nor_5_out_2, not_nor_6_out_2, or_nor_1_out_3;

  NOT_NOR not_nor_1 (.in_1(Lewy_czujnik), .out_2(not_nor_1_out_2));
  AND_NOR and_nor_1 (.in_1(not_nor_1_out_2), .in_2(Srodkowy_czujnik), .out_3(and_nor_1_out_3));
  AND_NOR and_nor_2 (.in_1(Lewy_czujnik), .in_2(not_nor_2_out_2), .out_3(and_nor_2_out_3));
  NOT_NOR not_nor_2 (.in_1(Srodkowy_czujnik), .out_2(not_nor_2_out_2));
  NOT_NOR not_nor_3 (.in_1(Lewy_czujnik), .out_2(not_nor_3_out_2));
  AND_NOR and_nor_3 (.in_1(not_nor_3_out_2), .in_2(not_nor_4_out_2), .out_3(and_nor_3_out_3));
  NOT_NOR not_nor_4 (.in_1(Srodkowy_czujnik), .out_2(not_nor_4_out_2));
  NOT_NOR not_nor_5 (.in_1(Srodkowy_czujnik), .out_2(not_nor_5_out_2));
  AND_NOR and_nor_4 (.in_1(not_nor_5_out_2), .in_2(Prawy_czujnik), .out_3(and_nor_4_out_3));
  NOT_NOR not_nor_6 (.in_1(Prawy_czujnik), .out_2(not_nor_6_out_2));
  OR_NOR or_nor_1 (.in_1(and_nor_1_out_3), .in_2(and_nor_2_out_3), .out_3(or_nor_1_out_3));
  OR_NOR or_nor_2 (.in_1(and_nor_3_out_3), .in_2(and_nor_4_out_3), .out_3(prawy_silnik));
  OR_NAND or_nand_1 (.in_1(or_nor_1_out_3), .in_2(not_nor_6_out_2), .out_3(lewy_silnik));
endmodule

module AND_NOR (
  input  in_1,
  input  in_2,
  output out_3
);

  wire nor_1_out, nor_2_out;

  nor nor_1 (nor_1_out, in_1, in_1);
  nor nor_2 (nor_2_out, in_2, in_2);
  nor nor_3 (out_3, nor_1_out, nor_2_out);
endmodule

module NOT_NOR (
  input  in_1,
  output out_2
);

  nor nor_1 (out_2, in_1, in_1);
endmodule

module OR_NOR (
  input  in_1,
  input  in_2,
  output out_3
);

  wire nor_1_out;

  nor nor_1 (nor_1_out, in_1, in_2);
  nor nor_2 (out_3, nor_1_out, nor_1_out);
endmodule

module NOR_NOR (
  input  in_1,
  input  in_2,
  output out_3
);

  nor nor_1 (out_3, in_1, in_2);
endmodule

module XOR_NOR (
  input  in_1,
  input  in_2,
  output out_3
);

  wire nor_1_out, nor_2_out, nor_3_out, nor_4_out, nor_5_out, nor_6_out, nor_7_out, nor_8_out, nor_9_out,
       nor_10_out, nor_11_out, nor_12_out, nor_13_out, nor_14_out, nor_15_out;

  nor nor_1 (nor_1_out, in_1, in_1);
  nor nor_2 (nor_2_out, nor_1_out, nor_3_out);
  nor nor_3 (nor_3_out, in_2, in_2);
  nor nor_4 (nor_4_out, nor_2_out, nor_2_out);
  nor nor_5 (nor_5_out, in_1, in_1);
  nor nor_6 (nor_6_out, nor_4_out, nor_4_out);
  nor nor_7 (nor_7_out, nor_4_out, nor_4_out);
  nor nor_8 (nor_8_out, in_2, in_2);
  nor nor_9 (nor_9_out, nor_5_out, nor_6_out);
  nor nor_10 (nor_10_out, nor_7_out, nor_8_out);
  nor nor_11 (nor_11_out, nor_9_out, nor_9_out);
  nor nor_12 (nor_12_out, nor_10_out, nor_10_out);
  nor nor_13 (nor_13_out, nor_11_out, nor_11_out);
  nor nor_14 (nor_14_out, nor_13_out, nor_15_out);
  nor nor_15 (nor_15_out, nor_12_out, nor_12_out);
  nor nor_16 (out_3, nor_14_out, nor_14_out);
endmodule

module NAND_XOR (
  input  in_1,
  input  in_2,
  output out_3
);

  wire nor_1_out, nor_2_out, nor_3_out;

  nor nor_1 (nor_1_out, in_1, in_1);
  nor nor_2 (nor_2_out, in_2, in_2);
  nor nor_3 (nor_3_out, nor_1_out, nor_2_out);
  nor nor_4 (out_3, nor_3_out, nor_3_out);
endmodule
