// Logisim project syc8.circ as structural Verilog: 3 circuits, main circuit main
module main (
  input  _0,
  input  _1,
  input  _2,
  input  _3,
  output out_5,
  output out_6
);

  wire not_1_out;

  Multiplexer #(.select(4)) multiplexer_1 (
    .in0(1'b1), .in1(1'b1), .in2(1'b0), .in3(1'b1), .in4(1'b0), .in5(1'b0), .in6(1'b0), .in7(1'b0),
    .in8(1'b1), .in9(1'b1), .in10(1'b1), .in11(1'b0), .in12(1'b0), .in13(1'b0), .in14(1'b0), .in15(1'b1),
    .out(out_6), .sel({_3, _2, _1, _0}));  // open: en
  not not_1 (not_1_out, _3);
  Multiplexer #(.select(3)) multiplexer_2 (
    .in0(1'b1), .in1(1'b1), .in2(_3), .in3(not_1_out), .in4(1'b0), .in5(1'b0), .in6(1'b0), .in7(_3),
    .out(out_5), .sel({_2, _1, _0}));  // open: en
endmodule

module u2 (
  input  [3:0] in_1,
  input  [3:0] in_2,
  output out_3,
  output [3:0] out_4
);

  wire adder_1_cout, adder_2_cout;

  Adder #(.width(3)) adder_1 (.a(in_1[2:0]), .b(in_2[2:0]), .out(out_4[2:0]), .cout(adder_1_cout));  // open: cin
  Adder #(.width(1)) adder_2 (.a(in_1[3]), .b(in_2[3]), .out(out_4[3]), .cin(adder_1_cout), .cout(adder_2_cout));
  xor xor_1 (out_3, adder_1_cout, adder_2_cout);
endmodule

module ALU (
  input  [3:0] in_1,
  input  [3:0] in_2,
  input  [1:0] in_3,
  output Z,
  output C,
  output [3:0] out_6
);

  wire [3:0] and_1_out, negator_1_out, u2_1_out_4, xor_1_out;

  u2 u2_1 (.in_1(in_1), .in_2(in_2), .out_3(C), .out_4(u2_1_out_4));
  Negator #(.width(4)) negator_1 (.in(in_2), .out(negator_1_out));
  assign xor_1_out = in_1 ^ in_2;  // XOR_Gate xor_1, 4 bits wide
  assign and_1_out = in_1 & in_2;  // AND_Gate and_1, 4 bits wide
  Multiplexer #(.select(2), .width(4)) multiplexer_1 (
    .in0(u2_1_out_4), .in1(negator_1_out), .in2(xor_1_out), .in3(and_1_out), .out(out_6), .sel(in_3));  // open: en
  Comparator #(.width(4)) comparator_1 (.a(4'b0000), .b(out_6), .eq(Z));  // open: gt, lt
endmodule
