// Logisim project syc9.circ as structural Verilog: 2 circuits, main circuit main
module main (
  input  in_1,
  input  in_2,
  output out_3,
  output out_4,
  output out_5,
  output out_6,
  output out_7
);

  wire and_1_out, and_2_out, clock_1_out, d_ff_1_q, d_ff_2_qn, d_ff_3_qn, d_ff_4_q, d_ff_5_qn, d_ff_6_qn,
       d_ff_7_q, d_ff_8_qn, d_ff_9_qn, d_ff_10_q, d_ff_10_qn, d_ff_11_qn, d_ff_12_qn, d_ff_13_q, d_ff_14_q,
       d_ff_15_q, d_ff_16_qn, xor_1_out;
  wire [3:0] d_ff_2_q, d_ff_3_q;

  Clock clock_1 (.out(clock_1_out));
  Hex_Digit_Display hex_digit_display_1 (.value(d_ff_2_q));  // open: dp
  Hex_Digit_Display hex_digit_display_2 (.value(d_ff_3_q));  // open: dp
  latch latch_1 (.dane(d_ff_1_q), .zatrzask(in_1), .out_3(out_3));
  D_Flip_Flop d_ff_1 (.clk(clock_1_out), .D(d_ff_10_qn), .Q(d_ff_1_q), .preset(in_2));  // open: Qn, en, reset
  D_Flip_Flop d_ff_2 (
    .clk(clock_1_out), .D(d_ff_2_qn), .Q(d_ff_2_q[0]), .Qn(d_ff_2_qn), .reset(and_1_out));  // open: preset, en
  and and_1 (and_1_out, d_ff_2_q[0], d_ff_2_q[3]);
  D_Flip_Flop d_ff_3 (
    .clk(clock_1_out), .D(d_ff_3_qn), .Q(d_ff_3_q[0]), .Qn(d_ff_3_qn), .preset(and_2_out));  // open: en, reset
  and and_2 (and_2_out, d_ff_3_q[1], d_ff_3_q[3]);
  D_Flip_Flop d_ff_4 (.clk(clock_1_out), .D(d_ff_1_q), .Q(d_ff_4_q), .reset(in_2));  // open: Qn, preset, en
  D_Flip_Flop d_ff_5 (
    .clk(d_ff_2_qn), .D(d_ff_5_qn), .Q(d_ff_2_q[1]), .Qn(d_ff_5_qn), .reset(and_1_out));  // open: preset, en
  D_Flip_Flop d_ff_6 (
    .clk(d_ff_3_qn), .D(d_ff_6_qn), .Q(d_ff_3_q[1]), .Qn(d_ff_6_qn), .preset(and_2_out));  // open: en, reset
  latch latch_2 (.dane(d_ff_4_q), .zatrzask(in_1), .out_3(out_4));
  D_Flip_Flop d_ff_7 (.clk(clock_1_out), .D(d_ff_4_q), .Q(d_ff_7_q), .reset(in_2));  // open: Qn, preset, en
  D_Flip_Flop d_ff_8 (
    .clk(d_ff_5_qn), .D(d_ff_8_qn), .Q(d_ff_2_q[2]), .Qn(d_ff_8_qn), .reset(and_1_out));  // open: preset, en
  D_Flip_Flop d_ff_9 (
    .clk(d_ff_6_qn), .D(d_ff_9_qn), .Q(d_ff_3_q[2]), .Qn(d_ff_9_qn), .reset(and_2_out));  // open: preset, en
  latch latch_3 (.dane(d_ff_7_q), .zatrzask(in_1), .out_3(out_5));
  latch latch_4 (.dane(d_ff_10_q), .zatrzask(in_1), .out_3(out_6));
  D_Flip_Flop d_ff_10 (
    .clk(clock_1_out), .D(d_ff_7_q), .Q(d_ff_10_q), .Qn(d_ff_10_qn), .reset(in_2));  // open: preset, en
  D_Flip_Flop d_ff_11 (
    .clk(d_ff_8_qn), .D(d_ff_11_qn), .Q(d_ff_2_q[3]), .Qn(d_ff_11_qn), .reset(and_1_out));  // open: preset, en
  D_Flip_Flop d_ff_12 (
    .clk(d_ff_9_qn), .D(d_ff_12_qn), .Q(d_ff_3_q[3]), .Qn(d_ff_12_qn), .reset(and_2_out));  // open: preset, en
  xor xor_1 (xor_1_out, d_ff_13_q, d_ff_16_qn);
  D_Flip_Flop d_ff_13 (.clk(clock_1_out), .D(xor_1_out), .Q(d_ff_13_q));  // open: Qn, preset, en, reset
  D_Flip_Flop d_ff_14 (.clk(clock_1_out), .D(d_ff_13_q), .Q(d_ff_14_q));  // open: Qn, preset, en, reset
  D_Flip_Flop d_ff_15 (.clk(clock_1_out), .D(d_ff_14_q), .Q(d_ff_15_q));  // open: Qn, preset, en, reset
  D_Flip_Flop d_ff_16 (.clk(clock_1_out), .D(d_ff_15_q), .Q(out_7), .Qn(d_ff_16_qn));  // open: preset, en, reset
endmodule

module latch (
  input  dane,
  input  zatrzask,
  output out_3
);

  wire nand_1_out, nand_2_out, nand_4_out, not_1_out;

  not not_1 (not_1_out, dane);
  nand nand_1 (nand_1_out, dane, zatrzask);
  nand nand_2 (nand_2_out, zatrzask, not_1_out);
  nand nand_3 (out_3, nand_1_out, nand_4_out);
  nand nand_4 (nand_4_out, out_3, nand_2_out);
endmodule
